# Fritzing sketch weatherstation (saved by Fritzing 0.9.2b)
circuit board: 8.46667cm x 5.64444cm
breadboards: 1

parts:
  Часть1 = Arduino Leonardo (Rev3b)
  Часть2 = Breadboard Power Supply Board SMD
  RHT1 = Humidity and Temperature Sensor RHT03
  Grove1 = Grove OLED 128x96
  Часть3 = Real Time Clock Module - DS1307 RTC Breakout Board
  Часть4 = Barometric Pressure Sensor - BMP085 Breakout

nets:
  N1: Часть1.D0/RX, Grove1.SDA, Часть3.SQW, Часть4.SCL
  N2: Часть1.D1/TX, Grove1.SCL, Часть3.SCL, Часть4.SDA
  VCC: Часть1.5V, Часть2.VCC, RHT1.Vcc, Grove1.VCC, Часть3.5V, Часть4.VCC
  GND: Часть1.GND, Часть2.GND, RHT1.GND_1, Grove1.GND, Часть3.GND, Часть4.GND
  N3: Часть1.D12/A11, RHT1.Data-signal
